# Fritzing sketch break_out-1_b (saved by Fritzing 0.9.4)
circuit board: 3.62178cm x 3.94919cm
breadboards: 1

parts:
  Socket = Ink_cartridge_breakout_V0.1
  AUX-OUT1 = double row female pin header, 14 pins [form="♀ (female)"]

nets:
  N1: Socket.Pin_1, AUX-OUT1.pin6
  N2: Socket.Pin_2, AUX-OUT1.pin8
  N3: Socket.Pin_3, AUX-OUT1.pin9
  N4: Socket.Pin_4, AUX-OUT1.pin10
  N5: Socket.Pin_5, AUX-OUT1.pin11
  N6: Socket.Pin_6, AUX-OUT1.pin12
  N7: Socket.pin_7, AUX-OUT1.pin13
  N8: Socket.pin_8, AUX-OUT1.pin5
  N9: Socket.pin_9, AUX-OUT1.pin4
  N10: Socket.pin_10, AUX-OUT1.pin3
  N11: Socket.pin_11, AUX-OUT1.pin2
  N12: Socket.pin_12, AUX-OUT1.pin1
  N13: Socket.pin_13, Socket.pin_14, AUX-OUT1.pin14

custom parts:
  Ink_cartridge_breakout_V0.1: This is a Ink cartrage breakout board for the HP C6602. I
