# Fritzing sketch ink_cart_v2 (saved by Fritzing 0.9.3b)
circuit board: 3.5cm x 3.73cm
breadboards: 1

parts:
  AUX-OUT2 = double row female pin header, 14 pins [form="♀ (female)"]
  Part1 = Ink_cartridge_breakout_V0.1

nets:
  N1: AUX-OUT2.pin1, Part1.pin_12
  N2: AUX-OUT2.pin2, Part1.pin_11
  N3: AUX-OUT2.pin3, Part1.pin_10
  N4: AUX-OUT2.pin4, Part1.pin_9
  N5: AUX-OUT2.pin5, Part1.pin_8
  N6: AUX-OUT2.pin6, Part1.Pin_1
  N7: AUX-OUT2.pin8, Part1.Pin_2
  N8: AUX-OUT2.pin9, Part1.Pin_3
  N9: AUX-OUT2.pin10, Part1.Pin_4
  N10: AUX-OUT2.pin11, Part1.Pin_5
  N11: AUX-OUT2.pin12, Part1.Pin_6
  N12: AUX-OUT2.pin13, Part1.pin_7
  N13: AUX-OUT2.pin14, Part1.pin_13, Part1.pin_14

notes:
  6602 Cart Socket
  Ink_Plot_V2
  12/2020
  Mike Beradino

custom parts:
  Ink_cartridge_breakout_V0.1: This is a Ink cartrage breakout board for the HP C6602. I
