# Fritzing sketch ink_plot_v2a (saved by Fritzing 0.9.3b)
circuit board: 5cm x 5cm
breadboards: 1

parts:
  ULN2603 = Darlington Driver [package=dil18]
  ULN2603_2 = Darlington Driver [package=dil18]
  R1 = Resistor [tolerance=±5% resistance=10k package=THT]
  J19 = female pin header, 2 pins [form="♀ (female)"]
  Pad306 = Pad [width=0.75 height=3.5 connect=center]  # not connected
  Pad307 = Pad [width=0.75 height=3.5 connect=center]
  Pad313 = Pad [width=0.75 height=3.5 connect=center]
  Pad316 = Pad [width=0.75 height=3.5 connect=center]  # not connected
  Pad317 = Pad [width=0.75 height=3.5 connect=center]
  Pad318 = Pad [width=0.75 height=3.5 connect=center]
  HP4067 = 74HC4067 [package=ssop24]
  J20 = female pin header, 2 pins [form="♀ (female)"]
  C1 = Ceramic Capacitor [capacitance=0.1µF package="200 mil [THT, multilayer]"]
  J21 = female pin header, 2 pins [form="♀ (female)"]
  J22 = female pin header, 2 pins [form="♀ (female)"]
  AUX-OUT = double row female pin header, 14 pins [form="♀ (female)"]
  Power = LED - 3mm [color="Red (633nm)" package="3 mm [THT]"]
  J23 = female pin header, 6 pins [form="♀ (female)"]
  Pad305 = Pad [width=0.75 height=3.5 connect=center]
  Pad323 = Pad [width=0.75 height=3.5 connect=center]
  Pad322 = Pad [width=0.75 height=3.5 connect=center]
  Pad321 = Pad [width=0.75 height=3.5 connect=center]
  Pad315 = Pad [width=0.75 height=3.5 connect=center]
  Pad320 = Pad [width=0.75 height=3.5 connect=center]
  Pad319 = Pad [width=0.75 height=3.5 connect=center]
  Pad314 = Pad [width=0.75 height=3.5 connect=center]
  Pad332 = Pad [width=0.75 height=3.5 connect=center]
  Pad309 = Pad [width=0.75 height=3.5 connect=center]
  Pad346 = Pad [width=4 height=4 connect=center]  # not connected
  Pad347 = Pad [width=4 height=4 connect=center]  # not connected

nets:
  N1: ULN2603.1, HP4067.CHAN0
  N2: ULN2603.2, HP4067.CHAN1
  N3: ULN2603.3, HP4067.CHAN2
  N4: ULN2603.4, HP4067.CHAN3
  N5: ULN2603.5, HP4067.CHAN4
  N6: ULN2603.6, HP4067.CHAN5
  N7: ULN2603.7, HP4067.CHAN6
  N8: ULN2603.8, HP4067.CHAN7
  N9: ULN2603.9, ULN2603_2.9, R1.Pin_0, J19.pin2, HP4067.GND, J20.pin1, C1.1, J21.pin1, J22.pin2
  N10: ULN2603.10, ULN2603_2.10, J19.pin1, HP4067.VCC, C1.0, J22.pin1, Power.anode
  N11: ULN2603.11, AUX-OUT.pin5, Pad322.pad
  N12: ULN2603.12, AUX-OUT.pin6, Pad321.pad
  N13: ULN2603.13, AUX-OUT.pin8, Pad315.pad
  N14: ULN2603.14, AUX-OUT.pin9, Pad320.pad
  N15: ULN2603.15, Pad317.pad, AUX-OUT.pin10
  N16: ULN2603.16, AUX-OUT.pin11, Pad319.pad
  N17: ULN2603.17, AUX-OUT.pin12, Pad314.pad
  N18: ULN2603.18, AUX-OUT.pin13, Pad309.pad
  N19: ULN2603_2.1, HP4067.CHAN8
  N20: ULN2603_2.2, HP4067.CHAN9
  N21: ULN2603_2.3, HP4067.CHAN10
  N22: ULN2603_2.4, HP4067.CHAN11
  N23: ULN2603_2.15, Pad313.pad, AUX-OUT.pin1
  N24: ULN2603_2.16, AUX-OUT.pin2, Pad305.pad
  N25: ULN2603_2.17, AUX-OUT.pin3, Pad323.pad
  N26: ULN2603_2.18, Pad307.pad, AUX-OUT.pin4
  N27: R1.Pin_1, HP4067.EN, Power.cathode, J23.pin6
  N28: Pad318.pad, J20.pin2, J21.pin2, AUX-OUT.pin14, Pad332.pad
  N29: HP4067.COM, J23.pin5
  N30: HP4067.S0, J23.pin1
  N31: HP4067.S1, J23.pin2
  N32: HP4067.S3, J23.pin4
  N33: HP4067.S2, J23.pin3

notes:
  -
  +
  Cartridge
  Ink
  ~18-24V DC
  Driver
  Mike Beradino
  Ink_Plot_V2
  12/2020
  5V
  GND
  OUT
  IN
  S0
  S2
  S3
  COM
  EN
  S1
